// Logisim project EXP01_1.circ as structural Verilog: 1 circuit, main circuit main
module main (
  input  A,
  input  B,
  output out_3,
  output out_4,
  output out_5
);

  not not_1 (out_5, A);
  and and_1 (out_3, A, B);
  or or_1 (out_4, A, B);
endmodule
