// Logisim project EXP02_1_1.circ as structural Verilog: 1 circuit, main circuit main
module main (
  input  S0,
  input  S1,
  input  C0,
  input  C1,
  input  C2,
  input  C3,
  output Z
);

  wire and_1_out, and_2_out, and_3_out, and_4_out, not_1_out, not_2_out;

  not not_1 (not_1_out, S0);
  not not_2 (not_2_out, S1);
  and and_1 (and_1_out, not_2_out, C0, not_1_out);
  and and_2 (and_2_out, not_2_out, C1, S0);
  and and_3 (and_3_out, S1, C2, not_1_out);
  and and_4 (and_4_out, S1, C3, S0);
  or or_1 (Z, and_1_out, and_2_out, and_3_out, and_4_out);
endmodule
