// Logisim project EXP02_1_2.circ as structural Verilog: 1 circuit, main circuit main
module main (
  input  S0,
  input  S1,
  input  C1_0,
  input  C1_1,
  input  C1_2,
  input  C1_3,
  input  C2_0,
  input  C2_1,
  input  C2_2,
  input  C2_3,
  input  C3_0,
  input  C3_1,
  input  C3_2,
  input  C3_3,
  input  C1_0_2,
  input  C1_0_3,
  input  C1_0_4,
  input  C1_0_5,
  output Z0,
  output Z1,
  output Z2,
  output Z3
);

  wire and_1_out, and_2_out, and_3_out, and_4_out, and_5_out, and_6_out, and_7_out, and_8_out, and_9_out,
       and_10_out, and_11_out, and_12_out, and_13_out, and_14_out, and_15_out, and_16_out, not_1_out,
       not_2_out;

  not not_1 (not_1_out, S0);
  not not_2 (not_2_out, S1);
  and and_1 (and_1_out, not_1_out, C1_0, not_2_out);
  and and_2 (and_2_out, not_1_out, C1_1, not_2_out);
  and and_3 (and_3_out, not_1_out, C1_2, not_2_out);
  and and_4 (and_4_out, not_1_out, C1_3, not_2_out);
  and and_5 (and_5_out, S0, C2_0, not_2_out);
  and and_6 (and_6_out, S0, C2_1, not_2_out);
  and and_7 (and_7_out, S0, C2_2, not_2_out);
  and and_8 (and_8_out, S0, C2_3, not_2_out);
  and and_9 (and_9_out, not_1_out, C3_0, S1);
  and and_10 (and_10_out, not_1_out, C3_1, S1);
  and and_11 (and_11_out, not_1_out, C3_2, S1);
  and and_12 (and_12_out, not_1_out, C3_3, S1);
  and and_13 (and_13_out, S0, C1_0_2, S1);
  and and_14 (and_14_out, S0, C1_0_3, S1);
  and and_15 (and_15_out, S0, C1_0_4, S1);
  and and_16 (and_16_out, S0, C1_0_5, S1);
  or or_1 (Z3, and_4_out, and_8_out, and_12_out, and_16_out);
  or or_2 (Z0, and_1_out, and_5_out, and_9_out, and_13_out);
  or or_3 (Z1, and_2_out, and_6_out, and_10_out, and_14_out);
  or or_4 (Z2, and_3_out, and_7_out, and_11_out, and_15_out);
endmodule
