// Logisim project EXP02_2.circ as structural Verilog: 1 circuit, main circuit main
module main (
  input  S0,
  input  S1,
  input  D,
  output C0,
  output C1,
  output C2,
  output C3
);

  wire not_1_out, not_2_out, or_1_out, or_2_out, or_3_out, or_4_out;

  not not_1 (not_1_out, S0);
  not not_2 (not_2_out, S1);
  or or_1 (or_1_out, not_1_out, not_2_out);
  or or_2 (or_2_out, S0, S1);
  or or_3 (or_3_out, not_1_out, S1);
  or or_4 (or_4_out, not_2_out, S0);
  or or_5 (C0, or_2_out, D);
  or or_6 (C1, or_3_out, D);
  or or_7 (C2, or_4_out, D);
  or or_8 (C3, or_1_out, D);
endmodule
