// Logisim project EXP03_1.circ as structural Verilog: 1 circuit, main circuit main
module main (
  input  G1,
  input  G2,
  input  D0,
  input  D1,
  input  D2,
  output Y0,
  output Y1,
  output Y2,
  output Y3,
  output Y4,
  output Y5,
  output Y6,
  output Y7
);

  wire and_1_out, not_1_out, not_2_out, not_3_out, not_4_out, not_5_out, not_6_out, not_7_out, not_8_out,
       not_9_out;

  not not_1 (not_1_out, G1);
  not not_2 (not_2_out, not_1_out);
  and and_1 (and_1_out, not_2_out, not_3_out);
  not not_3 (not_3_out, G2);
  not not_4 (not_4_out, D0);
  not not_5 (not_5_out, D1);
  not not_6 (not_6_out, D2);
  not not_7 (not_7_out, not_4_out);
  not not_8 (not_8_out, not_5_out);
  not not_9 (not_9_out, not_6_out);
  nand nand_1 (Y0, and_1_out, not_4_out, not_5_out, not_6_out);
  nand nand_2 (Y1, and_1_out, not_6_out, not_5_out, not_7_out);
  nand nand_3 (Y2, and_1_out, not_6_out, not_8_out, not_4_out);
  nand nand_4 (Y3, and_1_out, not_6_out, not_7_out, not_8_out);
  nand nand_5 (Y4, and_1_out, not_9_out, not_5_out, not_4_out);
  nand nand_6 (Y5, and_1_out, not_9_out, not_7_out, not_5_out);
  nand nand_7 (Y6, and_1_out, not_8_out, not_9_out, not_4_out);
  nand nand_8 (Y7, and_1_out, not_7_out, not_8_out, not_9_out);
endmodule
