// Logisim project EXP03_3.circ as structural Verilog: 1 circuit, main circuit main
module main (
  input  D6,
  input  D5,
  input  D4,
  input  D3,
  input  D2,
  input  D1,
  input  D0,
  output Y2,
  output Y1,
  output Y3
);

  nor nor_1 (Y2, D0, D1, D2, D3);
  nor nor_2 (Y1, D0, D1, D5, D4);
  nor nor_3 (Y3, D0, D4, D2, D6);
endmodule
