// Logisim project EXP07_1.circ as structural Verilog: 1 circuit, main circuit main
module main (
  input  in_1,
  input  en,
  input  in_3,
  output out_4,
  output out_5,
  output out_6
);

  wire and_1_out, clock_1_out;

  Clock clock_1 (.out(clock_1_out));
  J_K_Flip_Flop j_k_ff_1 (.J(in_1), .clk(clock_1_out), .K(in_1), .Q(out_4), .en(en), .reset(in_3));  // open: Qn, preset
  J_K_Flip_Flop j_k_ff_2 (
    .J(out_4), .clk(clock_1_out), .K(out_4), .Q(out_5), .en(en), .reset(in_3));  // open: Qn, preset
  and and_1 (and_1_out, out_4, out_5);
  J_K_Flip_Flop j_k_ff_3 (
    .J(and_1_out), .clk(clock_1_out), .K(and_1_out), .Q(out_6), .en(en), .reset(in_3));  // open: Qn, preset
endmodule
